# Fritzing sketch Valve Control Circuit (saved by Fritzing 0.9.4)
circuit board: 7cm x 7.4cm

parts:
  R1 = Resistor [tolerance=±5% resistance=1k package=THT]
  Q1 = Basic FET N-Channel [part_number=IRF540N package="TO220 [THT]"]
  D1 = Schottky Diode [part_number=1N5817 package="300 mil [THT]"]
  U1 = TLP621 [package=THT]
  R5 = Resistor [tolerance=±5% resistance=1k package=THT]
  U2 = TLP621 [package=THT]
  R6 = Resistor [tolerance=±5% resistance=4.7k package=THT]
  R7 = Resistor [tolerance=±5% resistance=10k package=THT]
  R8 = Resistor [tolerance=±5% resistance=10k package=THT]
  D2 = Schottky Diode [part_number=1N5817 package="300 mil [THT]"]
  Q2 = Basic FET N-Channel [part_number=IRF540N package="TO220 [THT]"]
  R9 = Resistor [tolerance=±5% resistance=1k package=THT]
  U3 = TLP621 [package=THT]
  R12 = Resistor [tolerance=±5% resistance=10k package=THT]
  R11 = Resistor [tolerance=±5% resistance=10k package=THT]
  R10 = Resistor [tolerance=±5% resistance=4.7k package=THT]
  D3 = Schottky Diode [part_number=1N5817 package="300 mil [THT]"]
  Q3 = Basic FET N-Channel [part_number=IRF540N package="TO220 [THT]"]
  U4 = TLP621 [package=THT]
  R13 = Resistor [tolerance=±5% resistance=1k package=THT]
  Q4 = Basic FET N-Channel [part_number=IRF540N package="TO220 [THT]"]
  R14 = Resistor [tolerance=±5% resistance=4.7k package=THT]
  R16 = Resistor [tolerance=±5% resistance=10k package=THT]
  R15 = Resistor [tolerance=±5% resistance=10k package=THT]
  D4 = Schottky Diode [part_number=1N5817 package="300 mil [THT]"]
  J1 = male pin header, 5 pins [form="♂ (male)"]
  R2 = Resistor [tolerance=±5% resistance=4.7k package=THT]
  LED4 = LED - 3mm [color="Green (570nm)" package="3 mm [THT]"]
  LED3 = LED - 3mm [color="Green (570nm)" package="3 mm [THT]"]
  LED2 = LED - 3mm [color="Green (570nm)" package="3 mm [THT]"]
  LED1 = LED - 3mm [color="Green (570nm)" package="3 mm [THT]"]
  J2 = male pin header, 2 pins [form="♂ (male)" part_number="24 VDC"]
  R4 = Resistor [tolerance=±5% resistance=10k package=THT]
  R3 = Resistor [tolerance=±5% resistance=10k package=THT]
  J3 = double row male pin header, 8 pins [form="♂ (male)"]

nets:
  N1: R1.Pin_0, J1.pin1
  N2: R1.Pin_1, U1.Pin_1
  N3: Q1.gate, U1.Pin_3, R4.Pin_0
  N4: Q1.drain, D1.anode, LED1.cathode, J3.pin1
  N5: Q1.source, R8.Pin_1, Q2.source, R12.Pin_1, Q3.source, Q4.source, R16.Pin_1, J2.pin2, R4.Pin_1
  N6: D1.cathode, R6.Pin_0, R7.Pin_0, D2.cathode, R11.Pin_0, R10.Pin_0, D3.cathode, R14.Pin_0, R15.Pin_0, D4.cathode, R2.Pin_0, J2.pin1, R3.Pin_0, J3.pin5, J3.pin6, J3.pin7, J3.pin8
  N7: U1.Pin_2, U2.Pin_2, U3.Pin_2, U4.Pin_2, J1.pin5
  N8: U1.Pin_4, R2.Pin_1
  N9: R5.Pin_0, J1.pin2
  N10: R5.Pin_1, U2.Pin_1
  N11: U2.Pin_4, R6.Pin_1
  N12: U2.Pin_3, R8.Pin_0, Q2.gate
  N13: R7.Pin_1, LED2.anode
  N14: D2.anode, Q2.drain, LED2.cathode, J3.pin2
  N15: R9.Pin_0, J1.pin3
  N16: R9.Pin_1, U3.Pin_1
  N17: U3.Pin_4, R10.Pin_1
  N18: U3.Pin_3, R12.Pin_0, Q3.gate
  N19: R11.Pin_1, LED3.anode
  N20: D3.anode, Q3.drain, LED3.cathode, J3.pin3
  N21: U4.Pin_1, R13.Pin_1
  N22: U4.Pin_4, R14.Pin_1
  N23: U4.Pin_3, Q4.gate, R16.Pin_0
  N24: R13.Pin_0, J1.pin4
  N25: Q4.drain, D4.anode, LED4.cathode, J3.pin4
  N26: R15.Pin_1, LED4.anode
  N27: LED1.anode, R3.Pin_1

notes:
  +VE
  GND
  1
  2
  3
  4
  Gary Twinn
  RPi Valve / Stepper Driver
  Input
  5 - 24V DC
  Output
  2020 V1.1
